# Fritzing sketch Project2_fritzing (saved by Fritzing 0.9.3b)
breadboards: 8
stripboards: 1

parts:
  J1 = T Cobbler Plus
  Part1 = Arduino Uno (Rev3)  # not connected
  Part2 = Arduino Uno (Rev3)
  Raspberry_Pi_1 = Raspberry Pi 3 [part_number=RPI-3-V1.2]
  GLCD_128x1 = 128 x 64 Graphic LCD
  Part3 = Arduino Prototyping Shield
  C1 = Ceramic Capacitor [capacitance=100nF package="100 mil [THT, multilayer]"]
  U1 = mystery part, 3 pins [chip_label="Hall Effect"]
  C2 = Ceramic Capacitor [capacitance=100nF package="100 mil [THT, multilayer]"]
  C3 = Ceramic Capacitor [capacitance=100nF package="100 mil [THT, multilayer]"]
  C4 = Ceramic Capacitor [capacitance=100nF package="100 mil [THT, multilayer]"]
  C5 = Ceramic Capacitor [capacitance=100nF package="100 mil [THT, multilayer]"]
  C6 = Ceramic Capacitor [capacitance=100nF package="100 mil [THT, multilayer]"]
  C7 = Ceramic Capacitor [capacitance=100nF package="100 mil [THT, multilayer]"]
  C8 = Ceramic Capacitor [capacitance=100nF package="100 mil [THT, multilayer]"]
  C9 = Ceramic Capacitor [capacitance=100nF package="100 mil [THT, multilayer]"]
  C10 = Ceramic Capacitor [capacitance=100nF package="100 mil [THT, multilayer]"]
  C11 = Ceramic Capacitor [capacitance=100nF package="100 mil [THT, multilayer]"]
  R1 = Resistor [tolerance=±5% resistance=10k package=THT]
  U2 = LCD-16X2 [package=lcd-16x2_noholes]
  C12 = Electrolytic Capacitor [capacitance=0.22mF package="100 mil [THT, electrolytic]"]
  R2 = Resistor [tolerance=±5% resistance=51 package=THT]
  R3 = Rotary Potentiometer (Small) [maximum_resistance=100kΩ package=THT]
  Part4 = Adafruit MMA8451 Accelerometer [part_number="Adafruit #2019"]
  Part5 = MPL3115A2 I2C Barometric Pressure, Altitude, Temperature Sensor
  KEYPAD1 = Membrane Matrix Keypad
  Part7 = Adafruit 4-channel I2C-safe Bi-directional Logic Level Converter [part_number="Adafruit #757"]
  Part8 = Adafruit 4-channel I2C-safe Bi-directional Logic Level Converter [part_number="Adafruit #757"]
  J2 = Piezo Speaker
  Q1 = NPN-Transistor [package="TO92 [THT]"]
  Q2 = NPN-Transistor [package="TO92 [THT]"]
  Q3 = NPN-Transistor [package="TO92 [THT]"]
  Q4 = NPN-Transistor [package="TO92 [THT]"]
  R4 = Photocell (LDR) [package=THT]
  J3 = Basic Force Sensing Resistor (FSR) [package=THT]
  S1 = Round Pushbutton
  S2 = Round Pushbutton
  R5 = Resistor [tolerance=±5% resistance=10 package="2512 [SMD]"]
  R6 = Resistor [tolerance=±5% resistance=10 package="2512 [SMD]"]
  R7 = Resistor [tolerance=±5% resistance=10 package="2512 [SMD]"]
  R8 = Resistor [tolerance=±5% resistance=10 package="2512 [SMD]"]
  R9 = Resistor [tolerance=±5% resistance=5.1k package="2512 [SMD]"]
  R10 = Resistor [tolerance=±5% resistance=5.1k package="2512 [SMD]"]
  R11 = Resistor [tolerance=±5% resistance=5.1k package="2512 [SMD]"]
  R12 = Resistor [tolerance=±5% resistance=5.1k package="2512 [SMD]"]
  U3 = Luxeon LED [package=luxeon]
  U4 = Luxeon LED [package=luxeon]
  U5 = Luxeon LED [package=luxeon]
  U6 = Luxeon LED [package=luxeon]
  R13 = Resistor [tolerance=±5% resistance=10k package="2512 [SMD]"]
  R14 = Resistor [tolerance=±5% resistance=10k package="2512 [SMD]"]
  R16 = Resistor [tolerance=±5% resistance=10k package="2512 [SMD]"]
  R17 = Resistor [tolerance=±5% resistance=10k package="2512 [SMD]"]
  U7 = OP37 - Low Noise, Precision, High Speed Op Amp [part_number=OP37]
  VCC2 = Battery block 9V
  R18 = Resistor [tolerance=±5% resistance=1k package="2512 [SMD]"]
  R19 = Resistor [tolerance=±5% resistance=10k package="2512 [SMD]"]
  VCC1 = Battery block 9V

nets:
  3V3: J1.3V3, Part4.+3V3
  N1: J1.SDA, Part4.SDA
  N2: J1.5.0V, C1.1, U1.pin3, R1.Pin_1
  N3: J1.SCL, Part4.SCL
  N4: J1.GND#5, C1.0, U1.pin1, C8.0
  N5: J1.#4, Part4.GND
  N6: J1.#27, KEYPAD1.7
  N7: J1.#22, KEYPAD1.6
  N8: J1.#25, U1.pin2, C2.1, R1.Pin_0
  N9: J1.#5, KEYPAD1.5
  N10: J1.#6, KEYPAD1.4
  N11: J1.#13, KEYPAD1.3
  N12: J1.#19, KEYPAD1.2
  N13: J1.#26, KEYPAD1.1
  3V3_2: J1.3.3V, Raspberry_Pi_1.3v3, Raspberry_Pi_1.3V3
  5V: J1.5V, Raspberry_Pi_1.5V
  N14: J1.GPIO_2, Raspberry_Pi_1.GPIO2
  N15: J1.GPIO_3, Raspberry_Pi_1.GPIO3
  N16: J1.GND#46, J1.GND#49, J1.GND#54, J1.GND#60, J1.GND#65, J1.GND#70, J1.GND#74, J1.GND#79, Raspberry_Pi_1.GND
  N17: J1.GPIO_4, Raspberry_Pi_1.GPIO4
  N18: J1.GPIO_14, Raspberry_Pi_1.GPIO14
  N19: J1.GPIO_15, Raspberry_Pi_1.GPIO15
  N20: J1.GPIO_17, Raspberry_Pi_1.GPIO17
  N21: J1.GPIO_18, Raspberry_Pi_1.GPIO18
  N22: J1.GPIO_27, Raspberry_Pi_1.GPIO27
  N23: J1.GPIO_22, Raspberry_Pi_1.GPIO22
  N24: J1.GPIO_23, Raspberry_Pi_1.GPIO23
  N25: J1.GPIO_24, Raspberry_Pi_1.GPIO24
  N26: J1.GPIO_10, Raspberry_Pi_1.GPIO10
  N27: J1.GPIO_9, Raspberry_Pi_1.GPIO9
  N28: J1.GPIO_25, Raspberry_Pi_1.GPIO25
  N29: J1.GPIO_11, Raspberry_Pi_1.GPIO11
  N30: J1.GPIO_8, Raspberry_Pi_1.GPIO8
  N31: J1.GPIO_7, Raspberry_Pi_1.GPIO7
  N32: J1.ID_SD, Raspberry_Pi_1.ID_SD
  N33: J1.ID_SC, Raspberry_Pi_1.ID_SC
  N34: J1.GPIO_5, Raspberry_Pi_1.GPIO5
  N35: J1.GPIO_6, Raspberry_Pi_1.GPIO6
  N36: J1.GPIO_12, Raspberry_Pi_1.GPIO12
  N37: J1.GPIO_13, Raspberry_Pi_1.GPIO13
  N38: J1.GPIO_19, Raspberry_Pi_1.GPIO19
  N39: J1.GPIO_16, Raspberry_Pi_1.GPIO16
  N40: J1.GPIO_26, Raspberry_Pi_1.GPIO26
  N41: J1.GPIO_20, Raspberry_Pi_1.GPIO20
  N42: J1.GPIO_21, Raspberry_Pi_1.GPIO21
  N43: Part2.A0, J3.pin_0, R17.Pin_0
  N44: Part2.GND, Q1.C, Q2.C, R13.Pin_1, R14.Pin_1, R16.Pin_1, R17.Pin_1
  N45: Part2.D2, S1.leg0, R14.Pin_0
  N46: Part2.D3_PWM, S2.leg0, R16.Pin_0
  N47: Part2.D4, R10.Pin_1
  N48: Part2.D5_PWM, R12.Pin_1
  N49: Part2.D6_PWM, R11.Pin_1
  N50: Part2.D7, R9.Pin_1
  N51: GLCD_128x1.1_Vss, Part3.3.3V, C12.-, Part8.HV
  GND: GLCD_128x1.2_Vdd, Part3.GND, U2.VSS, U2.R_W, U2.K, C12.+, R3.leg2, Part5.GND, Part7.GND, Part8.GND
  N52: GLCD_128x1.4_D/I, Part7.A2
  N53: GLCD_128x1.7_DB0, Part7.A3
  N54: GLCD_128x1.8_DB1, Part7.A4
  N55: GLCD_128x1.15_CS1, Part8.A1
  N56: GLCD_128x1.16_CS2, Part8.A2
  N57: Part3.A4, Part5.SDA
  N58: Part3.A5, Part5.SCL
  N59: Part3.D2, Part7.B1
  N60: Part3.D3, Part8.B2
  N61: Part3.D4, Part7.B4
  N62: Part3.D5, Part8.B1
  N63: Part3.D6, U2.DB7
  N64: Part3.D7, U2.DB6
  +5V: Part3.+5V, U2.VDD, R2.Pin_1, R3.leg1, Part5.VIN
  N65: Part3.D8, U2.DB5
  N66: Part3.D9, U2.DB4
  N67: Part3.D11, U2.E
  N68: Part3.D12, Part7.B3
  N69: Part3.D13, U2.RS
  N70: C2.0, C4.1
  N71: C3.0, C5.1
  N72: C3.1, C4.0
  N73: C5.0, C11.1
  N74: C6.0, C8.1
  N75: C6.1, C7.0
  N76: C7.1, C9.0
  N77: C9.1, C10.0
  N78: C10.1, C11.0
  N79: U2.VO, R3.wiper
  N80: U2.A, R2.Pin_0
  N81: J2.pin1, U7.-V, VCC2.-, R19.Pin_1
  N82: J2.pin2, U7.TRIM#1, R18.Pin_0
  N83: Q1.E, U6.A
  N84: Q1.B, R11.Pin_0
  N85: Q2.E, U3.C
  N86: Q2.B, R10.Pin_0
  N87: Q3.B, R9.Pin_0
  N88: Q3.C, U4.A, VCC1.-
  N89: Q4.E, U5.C
  N90: Q4.B, R12.Pin_0
  N91: R4.pin_0, J3.pin_1, S1.leg1, S2.leg1
  N92: R4.pin_1, R13.Pin_0
  N93: R5.Pin_0, R6.Pin_0, R7.Pin_0, R8.Pin_0, VCC1.+
  N94: R6.Pin_1, U5.S
  N95: R7.Pin_1, U4.S, U6.S
  N96: R8.Pin_1, U3.S
  N97: U7.-IN, R18.Pin_1, R19.Pin_0
  N98: U7.TRIM#8, VCC2.+

custom parts:
  T Cobbler Plus: The T-Cobbler Plus is an add on prototyping board from Adafruit specifically designed for the Raspberry Pi B+ that can break out all those tasty power, GPIO, I2C and SPI pins from the 40-pin header onto a solderless breadboard. This set will make "cobbling together" prototypes with the Pi super easy. The T-Cobbler Plus can plug into any solderless breadboard.
  Adafruit MMA8451 Accelerometer: So many accelerometers and so little time! We've expanded our accelerometer selection even more with this high-precision and inexpensive MMA8451 Triple-Axis Accelerometer w/ 14-bit ADC. You can detect motion, tilt and basic orientation with a digital accelerometer - and the MMA8451 is a great accelerometer to start with. It has a wide usage range, from +-2g up to +-8g yet is easy to use with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
  MPL3115A2 I2C Barometric Pressure, Altitude, Temperature Sensor: This pressure sensor from Freescale is a great low-cost sensing solution for precision measurement of barometric pressure and altitude. The MPL3115A2 has a typical 1.5 Pascal resolution, which can resolve altitude at 0.3 meters (compare to the BMP180 which can do 0.17m). It has some upsides compared to the BMP180, such as interrupt outputs for ultra-low power usage, and its also a heck of a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
  Membrane Matrix Keypad: Membrane Matrix 3x4 Keypad
  Adafruit 4-channel I2C-safe Bi-directional Logic Level Converter: Because the Arduino (and Basic Stamp) are 5V devices, and most modern sensors, displays, flash cards and modes are 3.3V-only, many makers find that they need to perform level shifting/conversion to protect the 3.3V device from 5V. We do have some other handy level shifters in the shop, from the DIP 74LVC245 to the fancy bi-directional TXB0108. However, neither of these are happy to work with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
